# Fritzing sketch EHP2 (saved by Fritzing 1.0.5)
breadboards: 1

parts:
  Mod1 = Raspberry Pi Pico
  C2 = Capacitor Polarized [package=cpol-radial-1000uf-25v]
  S5 = Pushbutton [package="[THT]"]
  IR2 = TSOP312.., 314.. [package=THT]
  DHT11_2 = DHT11 module
  LCD2 = LCD screen  # not connected
  LED2 = smd LED [color="Red (633nm)" package="0603 [SMD]"]
  LED3 = smd LED [color="Green (555nm)" package="0603 [SMD]"]
  LED5 = smd LED [color="Yellow (595nm)" package="0603 [SMD]"]
  R6 = Resistor [tolerance=±5% power=0.25W resistance=220 package=THT]
  J2 = Basic Servo
  R7 = Resistor [tolerance=±5% power=0.25W resistance=220 package=THT]
  S6 = Pushbutton [package="[THT]"]
  S7 = Pushbutton [package="[THT]"]
  S8 = Pushbutton [package="[THT]"]
  R8 = Resistor [tolerance=±5% power=0.25W resistance=220 package=THT]

nets:
  GND: Mod1.pin_3, Mod1.pin_8, Mod1.pin_13, Mod1.pin_18, Mod1.pin_23, Mod1.pin_28, Mod1.pin_33, Mod1.pin_38, Mod1.pin_42, C2.-, S5.Pin_1, S5.Pin_2, S5.Pin_3, S5.Pin_4, IR2.Vs, DHT11_2.GND, R6.Pin_1, J2.gnd, R7.Pin_1, S6.Pin_1, S6.Pin_2, S7.Pin_1, S7.Pin_2, S8.Pin_1, S8.Pin_2, R8.Pin_1
  N1: Mod1.pin_6, DHT11_2.DATA
  N2: Mod1.pin_7, IR2.GND
  N3: Mod1.pin_9, J2.pulse
  N4: Mod1.pin_19, S7.Pin_3, S7.Pin_4
  N5: Mod1.pin_21, LED2.anode
  N6: Mod1.pin_22, LED3.anode
  N7: Mod1.pin_24, LED5.anode
  N8: Mod1.pin_30, S8.Pin_3, S8.Pin_4
  N9: Mod1.pin_36, IR2.Data, DHT11_2.VCC
  N10: Mod1.pin_40, C2.+, J2.vcc
  N11: LED2.cathode, R7.Pin_0
  N12: LED3.cathode, R6.Pin_0
  N13: LED5.cathode, R8.Pin_0
  N14: S6.Pin_3, S6.Pin_4

notes:
  Pico Debug Probe

custom parts:
  Raspberry Pi Pico: Raspberry Pi Pico. Based around the RP2040 microcontroller the Pico is a low cost microcontroller device bringing Raspberry Pi quality, cost, and easy of use to the microcontroller space. Jan 2021, Split part in to two versions: tht (this one) and SMD. This one will drill holes for a .1 in header in pcb to allow plugging in the module as well as providing pads to solder the module to the top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
  DHT11 module: https://cdn-learn.adafruit.com/downloads/pdf/dht.pdf DHT11 black pcb module reference by:https://github.com/adafruit/Fritzing-Library/blob/master/parts/DHT11%20Humitidy%20and%20Temperature%20Sensor.fzpz
